# Fritzing sketch hardware_diagram (saved by Fritzing 0.9.10b)

parts:
  Mod1 = Raspberry Pi 4B
  DRV_1 = DRV 8825 Stepper Motor Carrier, High Current [part_number="DRV 8825"]
  DRV_2 = DRV 8825 Stepper Motor Carrier, High Current [part_number="DRV 8825"]
  M1 = Stepper Motor - Bipolar
  M2 = Stepper Motor - Bipolar
  HC-SR04_Sensor_2 = HC-SR04 Ultrasonic Distance Sensor
  HC-SR04_Sensor_4 = HC-SR04 Ultrasonic Distance Sensor
  C1 = Electrolytic Capacitor [capacitance=100μF voltage=35V package="0807 [SMD, electrolytic]"]
  R2 = 1 kΩ Resistor [package="1206 [SMD]"]
  U1 = SWITCH-SPST-2 [package=switch-spst-vertical]
  C2 = Electrolytic Capacitor [capacitance=100μF voltage=35V package="0807 [SMD, electrolytic]"]
  R3 = 2 kΩ Resistor [package="1206 [SMD]"]
  R4 = 1 kΩ Resistor [package="1206 [SMD]"]
  R10 = 2 kΩ Resistor [package="1206 [SMD]"]
  HC-SR04_Sensor_5 = HC-SR04 Ultrasonic Distance Sensor
  HC-SR04_Sensor_6 = HC-SR04 Ultrasonic Distance Sensor
  R11 = 1 kΩ Resistor [package="1206 [SMD]"]
  R12 = 1 kΩ Resistor [package="1206 [SMD]"]
  R13 = 2 kΩ Resistor [package="1206 [SMD]"]  # not connected
  R14 = 2 kΩ Resistor [package="1206 [SMD]"]
  Mod2 = Passive Buzzer
  VCC2 = 4 x AAA Battery Mount
  U2 = LIPO-2000mAh [package=lipo-2000]  # not connected
  U3 = TRANSCHIPTC5747 [package=camera_sfv24r-2st_2]  # not connected
  U4 = TRANSCHIPTC5747 [package=camera_sfv24r-2st_2]  # not connected

nets:
  N1: Mod1.3V3, DRV_1.RESET, DRV_1.SLEEP, DRV_2.RESET, DRV_2.SLEEP
  VCC: Mod1.5V, HC-SR04_Sensor_2.VCC, HC-SR04_Sensor_4.VCC, HC-SR04_Sensor_5.VCC, HC-SR04_Sensor_6.VCC, Mod2.S
  N2: Mod1.GPIO2, HC-SR04_Sensor_4.TRIG
  N3: Mod1.GPIO3, R2.Pin_0, R3.Pin_0
  GND: Mod1.GND, DRV_1.GROUND_LOG, DRV_2.OUT_2A, DRV_2.GROUND_LOG, M2.C, HC-SR04_Sensor_4.GND, R3.Pin_1, R10.Pin_1, HC-SR04_Sensor_5.GND, R14.Pin_0, Mod2.-
  N4: Mod1.GPIO4, HC-SR04_Sensor_2.TRIG
  N5: Mod1.GPIO14, DRV_1.MS1
  N6: Mod1.GPIO15, DRV_1.MS2
  N7: Mod1.GPIO17, Mod2.NC
  N8: Mod1.GPIO18, DRV_1.MS3
  N9: Mod1.GPIO22, R4.Pin_0, R10.Pin_0
  N10: Mod1.GPIO23, DRV_1.STEP
  N11: Mod1.GPIO24, DRV_1.DIRECTION
  N12: Mod1.GPIO9, Mod1.GPIO25, DRV_2.MS1
  N13: Mod1.GPIO8, DRV_2.MS2
  N14: Mod1.GPIO7, DRV_2.MS3
  N15: Mod1.ID_SD, Mod1.ID_SC, DRV_2.STEP
  N16: Mod1.GPIO12, DRV_2.DIRECTION
  N17: Mod1.GPIO16, HC-SR04_Sensor_6.TRIG
  N18: Mod1.GPIO26, HC-SR04_Sensor_5.TRIG
  N19: Mod1.GPIO20, R12.Pin_1
  N20: Mod1.GPIO21, R11.Pin_1
  N21: DRV_1.VOLTAGE_ST/_MT, DRV_2.VOLTAGE_ST/_MT, C1.+, U1.O, C2.+
  N22: DRV_1.GROUND_ST/_MT, DRV_1.OUT_2B, DRV_1.OUT_2A, DRV_1.OUT_1A, DRV_1.OUT_1B, DRV_2.GROUND_ST/_MT, M1.A, M1.C, M1.B, M1.D, VCC2.-
  N23: DRV_2.OUT_2B, DRV_2.VOLTAGE_DD, M2.A
  N24: DRV_2.OUT_1A, M2.B
  N25: DRV_2.OUT_1B, M2.D
  N26: HC-SR04_Sensor_2.ECHO, HC-SR04_Sensor_2.GND, R4.Pin_1
  N27: U1.P, VCC2.+

custom parts:
  1 kΩ Resistor: A generic resistor
  2 kΩ Resistor: A generic resistor
